# Fritzing sketch simpleLEDConnection (saved by Fritzing 0.9.2b)
breadboards: 1

parts:
  Raspberry_Pi1 = Raspberry Pi 2
  R1 = Resistor [tolerance=±5% resistance=220 package=THT]
  R2 = Resistor [tolerance=±5% resistance=220 package=THT]
  LED1 = LED - 5mm [color="Red (633nm)" package="5 mm [THT]"]
  LED2 = LED - 5mm [color="Green (570nm)" package="5 mm [THT]"]

nets:
  N1: Raspberry_Pi1.GPIO23, LED2.cathode
  N2: Raspberry_Pi1.GPIO18, LED1.cathode
  N3: Raspberry_Pi1.GND, R1.Pin_0, R2.Pin_0
  N4: R1.Pin_1, LED1.anode
  N5: R2.Pin_1, LED2.anode
